# Fritzing sketch CubeSchematic (saved by Fritzing 0.9.3b)
circuit board: 4.01861cm x 4.06656cm
breadboards: 1

parts:
  Bauteil1 = ws2812b [package="smd 2812b"]
  Bauteil2 = ws2812b [package="smd 2812b"]
  Bauteil3 = ws2812b [package="smd 2812b"]
  Bauteil4 = ws2812b [package="smd 2812b"]
  WeMos_D1_Mini1 = WeMos D1 Mini
  Bauteil5 = ws2812b [package="smd 2812b"]

nets:
  5V: Bauteil1.VDD, Bauteil2.VDD, Bauteil3.VDD, Bauteil4.VDD, WeMos_D1_Mini1.5V, Bauteil5.VDD
  N1: Bauteil1.DOUT, Bauteil5.DIN
  0V: Bauteil1.VSS, Bauteil2.VSS, Bauteil3.VSS, Bauteil4.VSS, WeMos_D1_Mini1.G, Bauteil5.VSS
  N2: Bauteil1.DIN, Bauteil2.DOUT
  N3: Bauteil2.DIN, Bauteil3.DOUT
  N4: Bauteil3.DIN, Bauteil4.DOUT
  N5: Bauteil4.DIN, WeMos_D1_Mini1.D0
